// Logisim project Full Adder.circ as structural Verilog
module _3_Bit_Adder_Sub (
  input  M,
  input  A0,
  input  A1,
  input  A2,
  input  B0,
  input  B1,
  input  B2,
  output S0,
  output S1,
  output S2,
  output overflow,
  output Carry
);

  wire F_A_2_carry_2, F_A_carry_2, xor_1_out, xor_2_out, xor_3_out;

  xor xor_1 (xor_1_out, M, B0);
  xor xor_2 (xor_2_out, M, B1);
  xor xor_3 (xor_3_out, M, B2);
  Full_Adder F_A (.Carry(M), .X(A0), .Y(xor_1_out), .Sum(S0), .Carry_2(F_A_carry_2));
  Full_Adder F_A_2 (.Carry(F_A_carry_2), .X(A1), .Y(xor_2_out), .Sum(S1), .Carry_2(F_A_2_carry_2));
  Full_Adder F_A_3 (.Carry(F_A_2_carry_2), .X(A2), .Y(xor_3_out), .Sum(S2), .Carry_2(Carry));
  xor xor_4 (overflow, F_A_2_carry_2, Carry);
endmodule

module _3_Bit_Adder (
  input  A0,
  input  A1,
  input  A2,
  input  B0,
  input  B1,
  input  B2,
  output S0,
  output S1,
  output S2,
  output overflow,
  output Carry
);

  wire F_A_2_carry_2, F_A_carry_2;

  Full_Adder F_A (.Carry(1'b0), .X(A0), .Y(B0), .Sum(S0), .Carry_2(F_A_carry_2));
  Full_Adder F_A_2 (.Carry(F_A_carry_2), .X(A1), .Y(B1), .Sum(S1), .Carry_2(F_A_2_carry_2));
  Full_Adder F_A_3 (.Carry(F_A_2_carry_2), .X(A2), .Y(B2), .Sum(S2), .Carry_2(Carry));
  xor xor_1 (overflow, F_A_2_carry_2, Carry);
endmodule

module _3_Bit_Multiplier_v1_0 (
  input  B2,
  input  B1,
  input  B0,
  input  A2,
  input  A1,
  input  A0,
  output out_7,
  output out_8,
  output Carry,
  output M4,
  output M3,
  output M2,
  output M1,
  output M0
);

  wire and_1_out, and_2_out, and_3_out, and_4_out, and_5_out, and_6_out, and_7_out, and_8_out,
       n3_bit_adder_2_carry, n3_bit_adder_2_s1, n3_bit_adder_2_s2;

  and and_1 (and_1_out, B1, A2);
  and and_2 (and_2_out, B2, A2);
  _3_Bit_Adder u_3_bit_adder_1 (
    .A0(n3_bit_adder_2_s1), .A1(n3_bit_adder_2_s2), .A2(n3_bit_adder_2_carry), .B0(and_3_out),
    .B1(and_1_out), .B2(and_2_out), .S0(M2), .S1(M3), .S2(M4), .overflow(out_8), .Carry(Carry));
  and and_3 (and_3_out, B0, A2);
  and and_4 (and_4_out, B2, A1);
  _3_Bit_Adder u_3_bit_adder_2 (
    .A0(and_7_out), .A1(and_8_out), .A2(1'b0), .B0(and_6_out), .B1(and_5_out), .B2(and_4_out), .S0(M1),
    .S1(n3_bit_adder_2_s1), .S2(n3_bit_adder_2_s2), .overflow(out_7), .Carry(n3_bit_adder_2_carry));
  and and_5 (and_5_out, B1, A1);
  and and_6 (and_6_out, B0, A1);
  and and_7 (and_7_out, B1, A0);
  and and_8 (and_8_out, B2, A0);
  and and_9 (M0, B0, A0);
endmodule

module _3_Bit_Multiplier_v2_0 (
  input  B2,
  input  A2,
  input  B1,
  input  B0,
  input  A1,
  input  A0,
  output Sign,
  output M3,
  output M2,
  output M1,
  output M0
);

  wire and_1_out, and_2_out, and_3_out, full_adder_2_carry_2;

  xor xor_1 (Sign, B2, A2);
  and and_1 (and_1_out, B1, A1);
  Full_Adder full_adder_1 (.Carry(full_adder_2_carry_2), .X(1'b0), .Y(and_1_out), .Sum(M2), .Carry_2(M3));
  and and_2 (and_2_out, B0, A1);
  and and_3 (and_3_out, B1, A0);
  Full_Adder full_adder_2 (.Carry(1'b0), .X(and_3_out), .Y(and_2_out), .Sum(M1), .Carry_2(full_adder_2_carry_2));
  and and_4 (M0, B0, A0);
endmodule

module _3_Bit_Multiplier_v3_0 (
  input  B2,
  input  B1,
  input  B0,
  input  A2,
  input  A1,
  input  A0,
  output Carry,
  output Overflow,
  output Sign,
  output M,
  output M2,
  output M1,
  output M0
);

  wire and_1_out, and_2_out, and_3_out, and_5_out, n3_bit_adder_1_carry, n3_bit_adder_2_carry,
       n3_bit_adder_2_s1, n3_bit_adder_2_s2, nand_1_out, nand_2_out, nand_3_out, nand_4_out;

  and and_1 (and_1_out, B2, A2);
  nand nand_1 (nand_1_out, B1, A2);
  _3_Bit_Adder u_3_bit_adder_1 (
    .A0(n3_bit_adder_2_s1), .A1(n3_bit_adder_2_s2), .A2(n3_bit_adder_2_carry), .B0(nand_3_out),
    .B1(nand_1_out), .B2(and_1_out), .S0(M2), .S1(M), .S2(Sign), .Carry(n3_bit_adder_1_carry));  // open: overflow
  xor xor_1 (Carry, 1'b1, n3_bit_adder_1_carry);
  xor xor_2 (Overflow, Carry, Sign);
  nand nand_2 (nand_2_out, B2, A1);
  _3_Bit_Adder u_3_bit_adder_2 (
    .A0(and_5_out), .A1(nand_4_out), .A2(1'b1), .B0(and_2_out), .B1(and_3_out), .B2(nand_2_out), .S0(M1),
    .S1(n3_bit_adder_2_s1), .S2(n3_bit_adder_2_s2), .Carry(n3_bit_adder_2_carry));  // open: overflow
  nand nand_3 (nand_3_out, B0, A2);
  and and_2 (and_2_out, B0, A1);
  and and_3 (and_3_out, B1, A1);
  nand nand_4 (nand_4_out, B2, A0);
  and and_4 (M0, B0, A0);
  and and_5 (and_5_out, B1, A0);
endmodule

module Full_Adder (
  input  Carry,
  input  X,
  input  Y,
  output Sum,
  output Carry_2
);

  wire and_1_out, and_2_out, xor_1_out;

  xor xor_1 (xor_1_out, X, Y);
  and and_1 (and_1_out, X, Y);
  xor xor_2 (Sum, xor_1_out, Carry);
  and and_2 (and_2_out, xor_1_out, Carry);
  or or_1 (Carry_2, and_2_out, and_1_out);
endmodule

module _3_Bit_Complement_Magnitude_Inverter (
  input  X2,
  input  X1,
  input  X0,
  output X2_2,
  output X1_2,
  output X0_2
);

  wire and_1_out, nor_1_out;

  nor nor_1 (nor_1_out, X1, X0);
  xor xor_1 (X2_2, X2, nor_1_out);
  and and_1 (and_1_out, X2, X0);
  xor xor_2 (X1_2, and_1_out, X1);

  assign X0_2 = X0;
endmodule
